# Fritzing sketch Schematics Source (saved by Fritzing 0.9.3b)
breadboards: 1

parts:
  part = Arduino Uno (Rev3)
  Analog_Pot = Rotary Potentiometer (Small) [maximum_resistance=100kΩ package=THT]
  Digital_Potentiometer = MCP41xxx [package=so08]
  Resistor = Resistor [tolerance=±5% resistance=220 package="0603 [SMD]"]
  LED = smd LED [color="Green (555nm)" package="0805 [SMD]"]
  IR_Receiver = A382X5 [package=THT]

nets:
  N1: part.A5/SCL, Analog_Pot.wiper
  N2: part.D10_PWM/SS, Digital_Potentiometer.CS
  N3: part.D11_PWM/MOSI, Digital_Potentiometer.DI
  N4: part.D13/SCK, Digital_Potentiometer.SCK
  N5: part.D3_PWM, IR_Receiver.Data
  N6: part.D5_PWM, LED.anode
  5V: part.5V, Analog_Pot.leg2, Digital_Potentiometer.VCC, IR_Receiver.Vs
  GND: part.GND, Analog_Pot.leg1, Digital_Potentiometer.GND, Resistor.Pin_0, IR_Receiver.GND
  N7: Resistor.Pin_1, LED.cathode

custom parts:
  A382X5: The A382X5 is a miniaturized receiver for infrared remote control systems.
